# Fritzing sketch PI_CODESYS_PLC_Circuit (saved by Fritzing 0.9.3b)
breadboards: 1

parts:
  A1 = Raspberry Pi 5
  U1 = 16-Channel Relay Module [package=relay-16ch]
  Generic_4x4_button_keypad1 = Generic 4x4 Keypad
  LED1 = LED - 5mm [color="Red (633nm)" package="5 mm [THT]"]
  LED2 = LED - 5mm [color="Red (633nm)" package="5 mm [THT]"]
  Power_plug1 = Power plug
  VCC1 = Battery

nets:
  N1: A1.3V3, Generic_4x4_button_keypad1.R1
  N2: A1.5V, A1.Fan-5V, U1.VCCOUT_5V
  GND: A1.GND, U1.GND, U1.OUT_GND, Power_plug1.GND
  N3: A1.GPIO17, Generic_4x4_button_keypad1.C1
  N4: A1.GPIO18, Generic_4x4_button_keypad1.C2
  N5: A1.GPIO27, Generic_4x4_button_keypad1.C4
  N6: A1.GPIO22, Generic_4x4_button_keypad1.C3
  N7: A1.GPIO23, U1.IN7
  N8: A1.GPIO24, U1.IN6
  VCC: U1.VCC, Power_plug1.VCC
  N9: U1.K6_NO, LED1.anode
  N10: U1.K6_COM, U1.K7_COM, VCC1.+
  N11: U1.K7_NO, LED2.anode
  N12: LED1.cathode, LED2.cathode, VCC1.-

custom parts:
  Raspberry Pi 5: The RPi5, a faster version of the awesome Raspberry Pi4B ARM Board with 40 pin gpio.
  16-Channel Relay Module: 16 channel relay module
  Generic 4x4 Keypad: generic 4x4 keypad 4 rows of four 6 mm tact switches cheap and nasty but works
